# Fritzing sketch Untitled Sketch-2p (saved by Fritzing 0.9.3b)

parts:
  HC-SR04_Sensor_1 = HC-SR04 Ultrasonic Distance Sensor
  Part1 = FC-28 Soil Hygrometer Module
  Part2 = FC-28 Soil Hygrometer Module - Probe
  U2 = 2-Channel 5v Relay Shield [package=relay-2ch5v10a]
  WATER_PUMP1 = water pump/motor
  Part3 = FC-28 Soil Hygrometer Module
  Part4 = FC-28 Soil Hygrometer Module - Probe
  PCB2 = RTC_DS1302_module
  MH-ET_LIVE_ESP32_DEVKIT1 = MH-ET LIVE ESP32 DEVKIT 38 pins
  A1 = DHT22 module
  Sensor1 = Gas Sensor Breakout Board
  Part5 = BH1750
  LCD2 = 1_7in tft lcd
  SIM800L_BO1 = SIM800L BO
  Mod1 = generic-ac-power-supply [package=THT]
  WATER_PUMP2 = water pump/motor

nets:
  VCC: HC-SR04_Sensor_1.VCC, Part1.VCC, U2.VCC, U2.K1-In, U2.K2-In, Part3.VCC, PCB2.VCC, MH-ET_LIVE_ESP32_DEVKIT1.5V, A1.+, Sensor1.5V, Part5.VCC, LCD2.pin2, SIM800L_BO1.PIN2, Mod1.pin3#2
  N1: HC-SR04_Sensor_1.TRIG, HC-SR04_Sensor_1.ECHO, MH-ET_LIVE_ESP32_DEVKIT1.IO14
  GND: HC-SR04_Sensor_1.GND, U2.GND, PCB2.GND, MH-ET_LIVE_ESP32_DEVKIT1.GND, A1.-, Sensor1.DOUT, Part5.GND, LCD2.pin_1, LCD2.pin_14, SIM800L_BO1.pin_6, Mod1.pin3#3, WATER_PUMP2.pin_1
  GND_2: Part1.GND, WATER_PUMP1.pin_1, Part3.GND
  N2: Part1.AO, MH-ET_LIVE_ESP32_DEVKIT1.IO35
  N3: Part1.POS, Part2.POS
  N4: Part1.NEG, Part2.NEG
  N5: U2.IN1, MH-ET_LIVE_ESP32_DEVKIT1.IO26
  N6: U2.IN2, MH-ET_LIVE_ESP32_DEVKIT1.IO27
  N7: U2.K1-Off, WATER_PUMP1.pin_2
  N8: U2.K2-Off, WATER_PUMP2.pin_2
  N9: Part3.AO, MH-ET_LIVE_ESP32_DEVKIT1.IO34
  N10: Part3.POS, Part4.POS
  N11: Part3.NEG, Part4.NEG
  N12: PCB2.RST, MH-ET_LIVE_ESP32_DEVKIT1.IO2
  N13: PCB2.DAT, MH-ET_LIVE_ESP32_DEVKIT1.IO4
  N14: PCB2.CLK, MH-ET_LIVE_ESP32_DEVKIT1.IO5
  N15: MH-ET_LIVE_ESP32_DEVKIT1.3V3, LCD2.pin_8
  N16: MH-ET_LIVE_ESP32_DEVKIT1.IO32, Sensor1.GND
  N17: MH-ET_LIVE_ESP32_DEVKIT1.IO33, LCD2.pin_6
  N18: MH-ET_LIVE_ESP32_DEVKIT1.IO25, LCD2.pin_5
  N19: MH-ET_LIVE_ESP32_DEVKIT1.IO13, A1.Out
  N20: MH-ET_LIVE_ESP32_DEVKIT1.IO23, LCD2.pin4
  N21: MH-ET_LIVE_ESP32_DEVKIT1.IO22, Part5.SCL
  N22: MH-ET_LIVE_ESP32_DEVKIT1.IO21, Part5.SDA
  N23: MH-ET_LIVE_ESP32_DEVKIT1.IO18, LCD2.pin3
  N24: MH-ET_LIVE_ESP32_DEVKIT1.IO17, SIM800L_BO1.pin_4, Mod1.pin2
  N25: MH-ET_LIVE_ESP32_DEVKIT1.IO16, SIM800L_BO1.pin_5
  N26: MH-ET_LIVE_ESP32_DEVKIT1.IO15, LCD2.pin_7

custom parts:
  FC-28 Soil Hygrometer Module: The FC-28 is a soil hygrometer module that uses the Texas Instruments LM393 comparator chip to provide an analog measurement of soil humidity. The digital output is high when soil moisture is over a certain threshold, as determined by adjusting the potentiometer.
  FC-28 Soil Hygrometer Module - Probe: The FC-28 is a soil hygrometer module that uses the Texas Instruments LM393 comparator chip to provide an analog measurement of soil humidity.
  2-Channel 5v Relay Shield: 2 Channel 5v Relay Shield w. 2x SPD-06VDC-SD-C
  water pump/motor: WATER PUMP BY ARDUBLOCKTR
  RTC_DS1302_module: Arduino module DS1302 SPI Real Time Clock
  MH-ET LIVE ESP32 DEVKIT 38 pins: http://mh.nodebb.com/topic/2/mh-et-live-esp32-devkit
  DHT22 module: DHT22 module. Pins VCC Data GND.
  Gas Sensor Breakout Board: Gas sensor breakout board. Input voltage is 5V. Sensor output is available in analog and digital.
  BH1750: Light Sensor
  1_7in tft lcd: This is the Zoll 1.77in spi lcd display. The 1.77" display has 128x160 color pixels.
  generic-ac-power-supply: Generic ac power supply module. Use as is, or customize the svgs to fit your particular device (as they are all different.) Provides AC input and single DC output. PCB is generic and will need modifications if you intend to do a pcb mount.
